# Fritzing sketch PlacaRobot (saved by Fritzing 0.9.2b)
circuit board: 8.46667cm x 5.64444cm
breadboards: 1

parts:
  Parte1 = Arduino Uno (Rev3)
  R1 = Resistor [tolerance=±5% resistance=1k package=THT]
  R2 = Resistor [tolerance=±5% resistance=560 package=THT]
  R3 = Resistor [tolerance=±5% resistance=220 package=THT]
  R4 = Photocell (LDR) [package=THT]
  J1 = female pin header, 2 pins [form="♀ (female)"]
  J2 = female pin header, 2 pins [form="♀ (female)"]
  J3 = female pin header, 2 pins [form="♀ (female)"]

nets:
  N1: Parte1.A0, R3.Pin_1, R4.pin_1
  N2: Parte1.D9_PWM, R1.Pin_0
  N3: Parte1.D12/MISO, J2.pin2
  N4: Parte1.D13/SCK, J3.pin1
  N5: Parte1.3V3, R4.pin_0
  N6: Parte1.5V, J1.pin2, J3.pin2
  N7: Parte1.GND, R2.Pin_1, R3.Pin_0, J2.pin1
  N8: R1.Pin_1, R2.Pin_0, J1.pin1
